# Fritzing sketch esp8266_udp_rs485 (saved by Fritzing 0.9.2b)

parts:
  YwRobot_Power_Supply1 = YwRobot Breadboard Power Supply [part_number=545043]
  U1 = ESP8266 ESP-01 Upgraded WiFi Module [part_number=ESP8266]
  RS485_module1 = RS485 Module (MAX3485)

nets:
  N1: YwRobot_Power_Supply1.VCC#5, RS485_module1.VCC
  N2: YwRobot_Power_Supply1.VCC#9, U1.VCC
  N3: YwRobot_Power_Supply1.GND#11, RS485_module1.GND
  N4: YwRobot_Power_Supply1.GND#13, U1.GND
  N5: U1.RXD, RS485_module1.RO
  N6: U1.GPIO_2, RS485_module1.RE, RS485_module1.DE
  N7: U1.TXD, RS485_module1.DI

notes:
  ESP-01S
  RS485/UART TTL module
  RX+
  RX–

custom parts:
  YwRobot Breadboard Power Supply: The YwRobot Breadboard Power Supply (MB-V2) has two power rails; they can be 5V or 3V3. Power to the module can be provided through the female USB socket or through the A10 (female) 2.1mm power jack.
  ESP8266 ESP-01 Upgraded WiFi Module: Upgraded Version ESP-01,all Flash are upgraded to 1M byte.Also support Cloud service remote transmission.
  RS485 Module (MAX3485): Commercially available RS485 to RS232 TTL Module
